// Logisim project lab5.circ as structural Verilog: 1 circuit, main circuit main
module main (
);

  wire and_1_out, and_2_out, clock_1_out, clock_2_out, nand_1_out, nand_2_out, nand_3_out, not_1_out,
       not_2_out, not_3_out, not_4_out, not_5_out, not_6_out, not_7_out, not_8_out, not_9_out, not_10_out,
       not_11_out, not_12_out, not_13_out, not_14_out, not_15_out;
  wire [3:0] T1_2_q, T1_q;

  not not_1 (not_1_out, T1_q[0]);
  not not_2 (not_2_out, T1_q[1]);
  not not_3 (not_3_out, T1_q[2]);
  not not_4 (not_4_out, T1_q[0]);
  not not_5 (not_5_out, T1_q[1]);
  and and_1 (and_1_out, not_1_out, not_2_out, not_3_out);
  and and_2 (and_2_out, not_4_out, not_5_out);
  not not_6 (not_6_out, T1_2_q[0]);
  not not_7 (not_7_out, T1_2_q[1]);
  not not_8 (not_8_out, T1_2_q[2]);
  not not_9 (not_9_out, T1_2_q[0]);
  not not_10 (not_10_out, T1_2_q[1]);
  not not_11 (not_11_out, T1_2_q[0]);
  nand nand_1 (nand_1_out, not_6_out, not_7_out, 1'b1, not_8_out);
  nand nand_2 (nand_2_out, not_9_out, 1'b1, not_10_out);
  nand nand_3 (nand_3_out, not_11_out, 1'b1);
  Clock clock_1 (.out(clock_1_out));
  not not_12 (not_12_out, nand_1_out);
  not not_13 (not_13_out, nand_2_out);
  not not_14 (not_14_out, nand_3_out);
  Clock clock_2 (.out(clock_2_out));
  not not_15 (not_15_out, T1_q[0]);
  T_Flip_Flop T4 (.clk(clock_1_out), .T(and_1_out), .Q(T1_q[3]));  // open: Qn, preset, reset, en
  T_Flip_Flop T3 (.clk(clock_1_out), .T(and_2_out), .Q(T1_q[2]));  // open: Qn, preset, reset, en
  T_Flip_Flop T2 (.clk(clock_1_out), .T(not_15_out), .Q(T1_q[1]));  // open: Qn, preset, reset, en
  T_Flip_Flop T1 (.clk(clock_1_out), .T(1'b1), .Q(T1_q[0]));  // open: Qn, preset, reset, en
  T_Flip_Flop T4_2 (.clk(clock_2_out), .T(not_12_out), .Q(T1_2_q[3]));  // open: Qn, preset, reset, en
  T_Flip_Flop T3_2 (.clk(clock_2_out), .T(not_13_out), .Q(T1_2_q[2]));  // open: Qn, preset, reset, en
  T_Flip_Flop T2_2 (.clk(clock_2_out), .T(not_14_out), .Q(T1_2_q[1]));  // open: Qn, preset, reset, en
  T_Flip_Flop T1_2 (.clk(clock_2_out), .T(1'b1), .Q(T1_2_q[0]));  // open: Qn, preset, reset, en
  // Probe on T1_q
  // Probe on T1_2_q
endmodule
